// Logisim project DEMULTIPLEXER.circ as structural Verilog: 1 circuit, main circuit main
module main (
  input  Din,
  input  E,
  input  [1:0] S1_S0
);

  wire demultiplexer_1_out0, demultiplexer_1_out2, demultiplexer_1_out3, undriven;

  Demultiplexer #(.select(2)) demultiplexer_1 (
    .out0(demultiplexer_1_out0), .out2(demultiplexer_1_out2), .out3(demultiplexer_1_out3), .in(Din),
    .sel(S1_S0), .en(E));  // open: out1
  LED led_1 (.in(demultiplexer_1_out0));
  LED led_2 (.in(demultiplexer_1_out2));
  LED led_3 (.in(demultiplexer_1_out3));
  LED led_4 (.in(undriven));
endmodule
