// Logisim project DEMULTIPLEXER2.circ as structural Verilog: 1 circuit, main circuit main
module main (
  input  Din,
  input  S1,
  input  S0,
  input  E
);

  wire and_1_out, and_2_out, and_3_out, and_4_out, not_1_out, not_2_out;

  not not_1 (not_1_out, S1);
  not not_2 (not_2_out, S0);
  and and_1 (and_1_out, E, not_2_out, not_1_out, Din);
  and and_2 (and_2_out, E, not_2_out, S1, Din);
  and and_3 (and_3_out, E, S0, not_1_out, Din);
  and and_4 (and_4_out, E, S0, S1, Din);
  LED led_1 (.in(and_1_out));
  LED led_2 (.in(and_2_out));
  LED led_3 (.in(and_3_out));
  LED led_4 (.in(and_4_out));

  // Notes on the sheet:
  //   S1'
  //   S0'
endmodule
