// Logisim project ADDR CIRCUITS.circ as structural Verilog: 1 circuit, main circuit main
module main (
  input  A,
  input  B,
  input  Cin,
  input  A_2,
  input  B_2
);

  wire and_1_out, and_2_out, and_3_out, and_4_out, or_1_out, undriven, undriven_2, xor_1_out, xor_2_out,
       xor_3_out;

  and and_1 (and_1_out, A_2, B_2);
  xor xor_1 (xor_1_out, A, B);
  and and_2 (and_2_out, A, B);
  xor xor_2 (xor_2_out, A_2, B_2);
  LED led_1 (.in(xor_1_out));
  LED led_2 (.in(and_2_out));
  xor xor_3 (xor_3_out, xor_2_out, Cin);
  LED led_3 (.in(xor_3_out));
  and and_3 (and_3_out, undriven_2, A_2);
  and and_4 (and_4_out, undriven, B_2);
  or or_1 (or_1_out, and_3_out, and_4_out, and_1_out);
  LED led_4 (.in(or_1_out));

  // Notes on the sheet:
  //   HALF ADDR
  //   S
  //   C
  //   FULL ADDR
  //   S
  //   Cout
endmodule
