// Logisim project BasicLogicGates.circ as structural Verilog: 1 circuit, main circuit main
module main (
  input  A,
  input  B,
  input  A_2,
  input  A_3,
  input  B_2,
  input  A_4,
  input  B_3,
  input  A_5,
  input  A_6,
  input  B_4,
  input  B_5,
  input  A_7,
  input  B_6
);

  wire and_1_out, nand_1_out, nor_1_out, not_1_out, or_1_out, xnor_1_out, xor_1_out;

  LED led_1 (.in(not_1_out));
  not not_1 (not_1_out, A_2);
  LED Y (.in(and_1_out));
  and and_1 (and_1_out, A_4, B_3);
  LED led_2 (.in(or_1_out));
  or or_1 (or_1_out, A_6, B_5);
  nand nand_1 (nand_1_out, A, B);
  LED led_3 (.in(nand_1_out));
  nor nor_1 (nor_1_out, A_3, B_2);
  LED led_4 (.in(nor_1_out));
  xor xor_1 (xor_1_out, A_5, B_4);
  LED led_5 (.in(xor_1_out));
  xnor xnor_1 (xnor_1_out, A_7, B_6);
  LED led_6 (.in(xnor_1_out));
endmodule
