// Logisim project MULTIPLEX.circ as structural Verilog: 1 circuit, main circuit main
module main (
  input  in_1,
  input  in_2,
  input  in_3,
  input  in_4,
  input  [1:0] in_5,
  input  in_6
);

  wire multiplexer_1_out, undriven;

  Multiplexer #(.select(2)) multiplexer_1 (
    .in0(in_1), .in1(in_2), .in2(in_3), .in3(in_4), .out(multiplexer_1_out), .sel(in_5), .en(undriven));
  LED led_1 (.in(multiplexer_1_out));
endmodule
